// Logisim project Real_Alu.circ as structural Verilog: 5 circuits, main circuit In_A AND In_B
module In_A_AND_In_B (
  input  [7:0] In_A,
  input  [7:0] In_B,
  output [7:0] Alu_out
);

  assign Alu_out = In_A & In_B;  // AND_Gate and_1, 8 bits wide
endmodule

module In_a_OR_In_B (
  input  [7:0] In_A,
  input  [7:0] In_B,
  output [7:0] Alu_Out
);

  assign Alu_Out = In_A | In_B;  // OR_Gate or_1, 8 bits wide
endmodule

module Not_In_B (
  input  [7:0] In_B,
  output [7:0] Alu_Out
);

  assign Alu_Out = ~In_B;  // NOT_Gate not_1, 8 bits wide
endmodule

module Shift_to_left (
  input  D0,
  input  D1,
  input  D2,
  input  D3,
  input  D4,
  input  D5,
  input  D6,
  input  D7,
  output S0,
  output S1,
  output S2,
  output S3,
  output S4,
  output S5,
  output S7,
  output S6
);

  wire and_1_out, and_3_out, and_5_out, and_8_out, and_10_out, and_12_out, and_14_out, x2, x3, x4, x5, x6, x7;

  and and_1 (and_1_out, D0, 1'b0);
  and and_2 (S0, 1'b1, D1);
  or or_1 (S1, and_1_out, x2);
  and and_3 (and_3_out, D5, 1'b0);
  and and_4 (x5, 1'b1, D5);
  or or_2 (S6, and_3_out, x7);
  and and_5 (and_5_out, D1, 1'b0);
  and and_6 (x2, 1'b1, D2);
  or or_3 (S2, and_5_out, x3);
  and and_7 (x6, 1'b1, D6);
  and and_8 (and_8_out, D2, 1'b0);
  or or_4 (S3, and_8_out, x4);
  and and_9 (S7, D6, 1'b0);
  and and_10 (and_10_out, D3, 1'b0);
  and and_11 (x3, 1'b1, D3);
  or or_5 (S4, and_10_out, x5);
  and and_12 (and_12_out, D7, 1'b1);
  or or_6 (x7, and_12_out, D7);
  and and_13 (x4, 1'b1, D4);
  and and_14 (and_14_out, D4, 1'b0);
  or or_7 (S5, and_14_out, x6);

  // Other names for the same wires on the sheet: _0 = D0; _1 = D1; _2 = D2; _3 = D3; _4 = D4; _5 = D5; _6 = D6;
  //   _7 = D7
endmodule

module Shift_to_right (
  input  D0,
  input  D1,
  input  D2,
  input  D3,
  input  D4,
  input  D5,
  input  D6,
  input  D7,
  output S0,
  output S1,
  output S2,
  output S3,
  output S4,
  output S5,
  output S7,
  output S6
);

  wire and_1_out, and_3_out, and_6_out, and_8_out, and_11_out, and_12_out, and_14_out, x2, x3, x4, x5, x6, x7;

  and and_1 (and_1_out, D0, 1'b1);
  and and_2 (S0, 1'b0, D1);
  or or_1 (S1, and_1_out, x2);
  and and_3 (and_3_out, D5, 1'b1);
  and and_4 (x5, 1'b0, D5);
  or or_2 (S6, and_3_out, x7);
  and and_5 (x2, 1'b0, D2);
  and and_6 (and_6_out, D1, 1'b1);
  or or_3 (S2, and_6_out, x3);
  and and_7 (x6, 1'b0, D6);
  and and_8 (and_8_out, D2, 1'b1);
  or or_4 (S3, and_8_out, x4);
  and and_9 (S7, D6, 1'b1);
  and and_10 (x3, 1'b0, D3);
  and and_11 (and_11_out, D3, 1'b1);
  or or_5 (S4, and_11_out, x5);
  and and_12 (and_12_out, D7, 1'b0);
  or or_6 (x7, and_12_out, D7);
  and and_13 (x4, 1'b0, D4);
  and and_14 (and_14_out, D4, 1'b1);
  or or_7 (S5, and_14_out, x6);

  // Other names for the same wires on the sheet: _0 = D0; _1 = D1; _2 = D2; _3 = D3; _4 = D4; _5 = D5; _6 = D6;
  //   _7 = D7
endmodule
